// Digital circuit 4 BIT GCD.dig as structural Verilog
module _4_BIT_GCD (
  input  [3:0] A,
  input  LOAD,
  input  CLK,
  input  RST,
  input  [3:0] B,
  output G3,
  output G2,
  output G1,
  output G0
);

  wire _7448_1_p10, _7448_1_p11, _7448_1_p12, _7448_1_p13, _7448_1_p14, _7448_1_p15, _7448_1_p16, not_1_out,
       or_1_out;
  wire [3:0] div_1_r, shift_update_reg_1_q3, shift_update_reg_2_q0;

  Shift_Update_Reg shift_update_reg_1 (
    .B0(shift_update_reg_2_q0[0]), .A0(A[0]), .CH(or_1_out), .CLK(CLK), .B1(shift_update_reg_2_q0[1]),
    .A1(A[1]), .B2(shift_update_reg_2_q0[2]), .A2(A[2]), .B3(shift_update_reg_2_q0[3]), .A3(A[3]), .CLR(RST),
    .PRE(1'b0), .LOAD(LOAD), .Q0(shift_update_reg_1_q3[0]), .Q1(shift_update_reg_1_q3[1]),
    .Q2(shift_update_reg_1_q3[2]), .Q3(shift_update_reg_1_q3[3]));
  Shift_Update_Reg shift_update_reg_2 (
    .B0(div_1_r[0]), .A0(B[0]), .CH(or_1_out), .CLK(CLK), .B1(div_1_r[1]), .A1(B[1]), .B2(div_1_r[2]),
    .A2(B[2]), .B3(div_1_r[3]), .A3(B[3]), .CLR(RST), .PRE(1'b0), .LOAD(LOAD), .Q0(shift_update_reg_2_q0[0]),
    .Q1(shift_update_reg_2_q0[1]), .Q2(shift_update_reg_2_q0[2]), .Q3(shift_update_reg_2_q0[3]));
  or or_1 (or_1_out, shift_update_reg_2_q0[3], shift_update_reg_2_q0[2], shift_update_reg_2_q0[1], shift_update_reg_2_q0[0]);
  not not_1 (not_1_out, or_1_out);
  Div #(.Bits(4)) div_1 (.a(shift_update_reg_1_q3), .b(shift_update_reg_2_q0), .r(div_1_r));  // open: q
  Shift_Update_Reg shift_update_reg_3 (
    .B0(1'b0), .A0(shift_update_reg_1_q3[0]), .CH(1'b0), .CLK(CLK), .B1(1'b0), .A1(shift_update_reg_1_q3[1]),
    .B2(1'b0), .A2(shift_update_reg_1_q3[2]), .B3(1'b0), .A3(shift_update_reg_1_q3[3]), .CLR(1'b0),
    .PRE(1'b0), .LOAD(not_1_out), .Q0(G0), .Q1(G1), .Q2(G2), .Q3(G3));
  // _7448 _7448_1: pin names not known; wires that end beside it: G0, G1, G2, G3, 1'b1, 1'b1, 1'b1, 1'b0, 1'b1, _7448_1_p10, _7448_1_p11, _7448_1_p12, _7448_1_p13, _7448_1_p14, _7448_1_p15, _7448_1_p16
  Seven_Seg seven_seg_1 (
    .a(_7448_1_p10), .b(_7448_1_p11), .c(_7448_1_p12), .d(_7448_1_p13), .e(_7448_1_p14), .f(_7448_1_p15),
    .g(_7448_1_p16), .dp(1'b0));
endmodule
