// Digital circuit Shift_Update_Reg.dig as structural Verilog
module Shift_Update_Reg (
  input  B0,
  input  A0,
  input  CH,
  input  CLK,
  input  B1,
  input  A1,
  input  B2,
  input  A2,
  input  B3,
  input  A3,
  input  CLR,
  input  PRE,
  input  LOAD,
  output Q0,
  output Q1,
  output Q2,
  output Q3
);

  wire multiplexer_1_out, multiplexer_2_out, multiplexer_3_out, multiplexer_4_out, multiplexer_5_out,
       multiplexer_6_out, multiplexer_7_out, multiplexer_8_out;

  Multiplexer multiplexer_1 (.sel(CH), .in_0(A0), .in_1(B0), .out(multiplexer_1_out));
  Multiplexer multiplexer_2 (.sel(LOAD), .in_0(Q0), .in_1(multiplexer_1_out), .out(multiplexer_2_out));
  D_FF_AS d_ff_as_1 (.Set(PRE), .D(multiplexer_2_out), .C(CLK), .Clr(CLR), .Q(Q0));  // open: nQ
  Multiplexer multiplexer_3 (.sel(CH), .in_0(A1), .in_1(B1), .out(multiplexer_3_out));
  Multiplexer multiplexer_4 (.sel(LOAD), .in_0(Q1), .in_1(multiplexer_3_out), .out(multiplexer_4_out));
  D_FF_AS d_ff_as_2 (.Set(PRE), .D(multiplexer_4_out), .C(CLK), .Clr(CLR), .Q(Q1));  // open: nQ
  Multiplexer multiplexer_5 (.sel(CH), .in_0(A2), .in_1(B2), .out(multiplexer_5_out));
  Multiplexer multiplexer_6 (.sel(LOAD), .in_0(Q2), .in_1(multiplexer_5_out), .out(multiplexer_6_out));
  D_FF_AS d_ff_as_3 (.Set(PRE), .D(multiplexer_6_out), .C(CLK), .Clr(CLR), .Q(Q2));  // open: nQ
  Multiplexer multiplexer_7 (.sel(CH), .in_0(A3), .in_1(B3), .out(multiplexer_7_out));
  Multiplexer multiplexer_8 (.sel(LOAD), .in_0(Q3), .in_1(multiplexer_7_out), .out(multiplexer_8_out));
  D_FF_AS d_ff_as_4 (.Set(PRE), .D(multiplexer_8_out), .C(CLK), .Clr(CLR), .Q(Q3));  // open: nQ
endmodule
